# Fritzing sketch fritzing (saved by Fritzing 0.9.3b)

parts:
  Part1 = Arduino Pro Mini v13
  MOTOR1 = Vibration Motor
  Part3 = Adafruit FONA - Mini Cellular GSM Breakout
  BAT1 = Battery Holders [package=lipo-1100mAh]
  SP1 = SPEAKER [package=pcb_mount_speaker]
  MIC1 = Microphone
  S1 = Toggle Switch [package=THT]

nets:
  N1: Part1.RAW, S1.COM
  GND: Part1.GND, Part3.GND, BAT1.-
  N2: Part1.VCC, Part3.VCCIO
  N3: Part1.D13/SCK, Part3.RXD_5V
  N4: Part1.D4, Part3.RESET_5V
  N5: Part1.D3_PWM, Part3.TXD_5V
  N6: Part1.D2, Part3.RI_5V
  N7: MOTOR1.POS, Part3.Bz+
  N8: MOTOR1.NEG, Part3.Bz-
  N9: Part3.SPEAKER2-, SP1.+
  N10: Part3.SPEAKER2+, SP1.-
  N11: Part3.MIC2+, MIC1.pin2
  N12: Part3.MIC2-, MIC1.pin1
  N13: BAT1.+, S1.L1

custom parts:
  Vibration Motor: An eccentric vibration motor!
  Adafruit FONA - Mini Cellular GSM Breakout: An all-in-one cellular phone module that lets you add voice, text, SMS and GPRS data to your project. Quad-band 850/900/1800/1900MHz - connect onto any global GSM network with any 2G SIM. Includes an onboard LiPoly battery charging circuitry so you can take your project on the go. Also works as an FM radio receiver.
